// Logisim project Project1.circ as structural Verilog
module seconds (
  input  CLK,
  input  PWR,
  input  [7:0] value,
  input  set,
  output Carry,
  output [7:0] OUTBITS
);

  wire _0, _1, _2, _3, _4, _5, _6, _7, _59_out, and_1_out, and_2_out, and_3_out, and_4_out, and_5_out,
       and_7_out, clear, comparator_1_lt, d_ff_9_q, xor_1_out, xor_2_out, xor_3_out, xor_4_out, xor_5_out,
       xor_6_out, xor_7_out, xor_8_out, xor_9_out, xor_10_out, xor_11_out, xor_12_out, xor_13_out;

  D_Flip_Flop d_ff_1 (.clk(CLK), .D(xor_1_out), .Q(OUTBITS[0]), .preset(_0), .reset(clear));  // open: Qn, en
  xor xor_1 (xor_1_out, PWR, OUTBITS[0]);
  xor xor_2 (xor_2_out, OUTBITS[0], OUTBITS[1]);
  D_Flip_Flop d_ff_2 (.clk(CLK), .D(xor_2_out), .Q(OUTBITS[1]), .preset(_1), .reset(clear));  // open: Qn, en
  and and_1 (and_1_out, OUTBITS[1], OUTBITS[0]);
  Comparator #(.mode("unsigned")) comparator_1 (.a(value), .b(8'h3c), .lt(comparator_1_lt));  // open: gt, eq
  D_Flip_Flop d_ff_3 (.clk(CLK), .D(xor_3_out), .Q(OUTBITS[2]), .preset(_2), .reset(clear));  // open: Qn, en
  xor xor_3 (xor_3_out, xor_4_out, _59_out);
  xor xor_4 (xor_4_out, and_1_out, OUTBITS[2]);
  and and_2 (and_2_out, OUTBITS[2], OUTBITS[1], OUTBITS[0]);
  xor xor_5 (xor_5_out, xor_6_out, _59_out);
  xor xor_6 (xor_6_out, and_2_out, OUTBITS[3]);
  and and_3 (and_3_out, OUTBITS[3], OUTBITS[2], OUTBITS[1], OUTBITS[0]);
  D_Flip_Flop d_ff_4 (.clk(CLK), .D(xor_5_out), .Q(OUTBITS[3]), .preset(_3), .reset(clear));  // open: Qn, en
  xor xor_7 (xor_7_out, and_3_out, OUTBITS[4]);
  D_Flip_Flop d_ff_5 (.clk(CLK), .D(xor_8_out), .Q(OUTBITS[4]), .preset(_4), .reset(clear));  // open: Qn, en
  xor xor_8 (xor_8_out, xor_7_out, _59_out);
  and and_4 (and_4_out, OUTBITS[4], OUTBITS[3], OUTBITS[2], OUTBITS[1], OUTBITS[0]);
  xor xor_9 (xor_9_out, and_4_out, OUTBITS[5]);
  xor xor_10 (xor_10_out, xor_9_out, _59_out);
  and and_5 (and_5_out, OUTBITS[5], OUTBITS[4], OUTBITS[3], OUTBITS[2], OUTBITS[1], OUTBITS[0]);
  xor xor_11 (xor_11_out, and_5_out, OUTBITS[6]);
  and and_6 (clear, comparator_1_lt, set);
  D_Flip_Flop d_ff_6 (.clk(CLK), .D(xor_10_out), .Q(OUTBITS[5]), .preset(_5), .reset(clear));  // open: Qn, en
  and and_7 (and_7_out, OUTBITS[6], OUTBITS[5], OUTBITS[4], OUTBITS[3], OUTBITS[2], OUTBITS[1], OUTBITS[0]);
  D_Flip_Flop d_ff_7 (.clk(CLK), .D(xor_11_out), .Q(OUTBITS[6]), .preset(_6), .reset(clear));  // open: Qn, en
  xor xor_12 (xor_12_out, and_7_out, OUTBITS[7]);
  Multiplexer #(.width(8)) multiplexer_1 (
    .in0({8{1'b0}}), .in1(value), .out({_7, _6, _5, _4, _3, _2, _1, _0}), .sel(clear));  // open: en
  D_Flip_Flop d_ff_8 (.clk(CLK), .D(xor_12_out), .Q(OUTBITS[7]), .preset(_7), .reset(clear));  // open: Qn, en
  xor xor_13 (xor_13_out, CLK, d_ff_9_q);
  and _59 (_59_out, ~OUTBITS[7], ~OUTBITS[6], OUTBITS[5], OUTBITS[4], OUTBITS[3], ~OUTBITS[2], OUTBITS[1], OUTBITS[0]);  // AND_Gate
  // Probe on OUTBITS
  and and_8 (Carry, CLK, d_ff_9_q);
  D_Flip_Flop d_ff_9 (.clk(xor_13_out), .D(_59_out), .Q(d_ff_9_q));  // open: Qn, preset, en, reset
endmodule

module test__not_used (
  input  PWR,
  input  CLK,
  output [7:0] SEC,
  output Carry
);

  wire _59_out, and_1_out, and_2_out, and_3_out, and_4_out, and_5_out, and_6_out, or_1_out, or_2_out,
       or_3_out, xor_1_out;

  J_K_Flip_Flop j_k_ff_1 (.J(SEC[0]), .clk(CLK), .K(SEC[0]), .Q(SEC[1]));  // open: Qn, preset, en, reset
  J_K_Flip_Flop j_k_ff_2 (.J(PWR), .clk(CLK), .K(PWR), .Q(SEC[0]));  // open: Qn, preset, en, reset
  and and_1 (and_1_out, SEC[1], SEC[0]);
  xor xor_1 (xor_1_out, and_1_out, _59_out);
  and and_2 (and_2_out, SEC[2], SEC[1], SEC[0]);
  or or_1 (or_1_out, and_2_out, _59_out);
  J_K_Flip_Flop j_k_ff_3 (.J(xor_1_out), .clk(CLK), .K(xor_1_out), .Q(SEC[2]));  // open: Qn, preset, en, reset
  and and_3 (and_3_out, SEC[3], SEC[2], SEC[1], SEC[0]);
  or or_2 (or_2_out, and_3_out, _59_out);
  J_K_Flip_Flop j_k_ff_4 (.J(or_1_out), .clk(CLK), .K(or_1_out), .Q(SEC[3]));  // open: Qn, preset, en, reset
  J_K_Flip_Flop j_k_ff_5 (.J(or_2_out), .clk(CLK), .K(or_2_out), .Q(SEC[4]));  // open: Qn, preset, en, reset
  and and_4 (and_4_out, SEC[4], SEC[3], SEC[2], SEC[1], SEC[0]);
  or or_3 (or_3_out, and_4_out, _59_out);
  J_K_Flip_Flop j_k_ff_6 (.J(or_3_out), .clk(CLK), .K(or_3_out), .Q(SEC[5]));  // open: Qn, preset, en, reset
  and and_5 (and_5_out, SEC[5], SEC[4], SEC[3], SEC[2], SEC[1], SEC[0]);
  J_K_Flip_Flop j_k_ff_7 (.J(and_5_out), .clk(CLK), .K(and_5_out), .Q(SEC[6]));  // open: Qn, preset, en, reset
  and and_6 (and_6_out, SEC[6], SEC[5], SEC[4], SEC[3], SEC[2], SEC[1], SEC[0]);
  J_K_Flip_Flop j_k_ff_8 (.J(and_6_out), .clk(CLK), .K(and_6_out), .Q(SEC[7]));  // open: Qn, preset, en, reset
  and _59 (_59_out, ~SEC[7], ~SEC[6], SEC[5], SEC[4], SEC[3], ~SEC[2], SEC[1], SEC[0]);  // AND_Gate
  and and_7 (Carry, _59_out, CLK);
endmodule

module hours (
  input  CLK,
  input  PWR,
  input  _12_hr,
  input  [7:0] value,
  input  set,
  output PM,
  output Carry,
  output [7:0] OUTBITS
);

  wire _0, _1, _2, _3, _4, _5, _6, _7, _8, _11_out, _23_out, and_1_out, and_2_out, and_3_out, and_4_out,
       and_5_out, and_6_out, clear, comparator_1_lt, d_ff_10_q, or_1_out, xor_1_out, xor_2_out, xor_3_out,
       xor_4_out, xor_5_out, xor_6_out, xor_7_out, xor_8_out, xor_9_out, xor_10_out, xor_11_out, xor_12_out;
  wire [3:2] _0_out;
  wire [7:0] adder_1_out, d_ff_1_q, subtractor_1_out, undriven;

  xor xor_1 (xor_1_out, PWR, d_ff_1_q[0]);
  D_Flip_Flop d_ff_1 (.clk(CLK), .D(xor_1_out), .Q(d_ff_1_q[0]), .preset(_0), .reset(clear));  // open: Qn, en
  xor xor_2 (xor_2_out, d_ff_1_q[0], d_ff_1_q[1]);
  D_Flip_Flop d_ff_2 (.clk(CLK), .D(xor_2_out), .Q(d_ff_1_q[1]), .preset(_1), .reset(clear));  // open: Qn, en
  and and_1 (and_1_out, d_ff_1_q[1], d_ff_1_q[0]);
  D_Flip_Flop d_ff_3 (.clk(CLK), .D(xor_3_out), .Q(d_ff_1_q[2]), .preset(_2), .reset(clear));  // open: Qn, en
  xor xor_3 (xor_3_out, and_1_out, d_ff_1_q[2]);
  xor xor_4 (xor_4_out, xor_5_out, _23_out);
  and and_2 (and_2_out, d_ff_1_q[2], d_ff_1_q[1], d_ff_1_q[0]);
  xor xor_5 (xor_5_out, and_2_out, d_ff_1_q[3]);
  Comparator #(.mode("unsigned")) comparator_1 (.a(value), .b(8'h18), .lt(comparator_1_lt));  // open: gt, eq
  Comparator #(.mode("unsigned")) comparator_2 (.a(value), .b(8'hb), .gt(_8));  // open: eq, lt
  D_Flip_Flop d_ff_4 (.clk(CLK), .D(xor_4_out), .Q(d_ff_1_q[3]), .preset(_3), .reset(clear));  // open: Qn, en
  and and_3 (and_3_out, d_ff_1_q[3], d_ff_1_q[2], d_ff_1_q[1], d_ff_1_q[0]);
  xor xor_6 (xor_6_out, and_3_out, d_ff_1_q[4]);
  xor xor_7 (xor_7_out, xor_6_out, _23_out);
  and and_4 (and_4_out, d_ff_1_q[4], d_ff_1_q[3], d_ff_1_q[2], d_ff_1_q[1], d_ff_1_q[0]);
  xor xor_8 (xor_8_out, and_4_out, d_ff_1_q[5]);
  D_Flip_Flop d_ff_5 (.clk(CLK), .D(xor_7_out), .Q(d_ff_1_q[4]), .preset(_4), .reset(clear));  // open: Qn, en
  and and_5 (and_5_out, d_ff_1_q[5], d_ff_1_q[4], d_ff_1_q[3], d_ff_1_q[2], d_ff_1_q[1], d_ff_1_q[0]);
  D_Flip_Flop d_ff_6 (.clk(CLK), .D(xor_8_out), .Q(d_ff_1_q[5]), .preset(_5), .reset(clear));  // open: Qn, en
  xor xor_9 (xor_9_out, and_5_out, d_ff_1_q[6]);
  and and_6 (and_6_out, d_ff_1_q[6], d_ff_1_q[5], d_ff_1_q[4], d_ff_1_q[3], d_ff_1_q[2], d_ff_1_q[1], d_ff_1_q[0]);
  D_Flip_Flop d_ff_7 (.clk(CLK), .D(xor_9_out), .Q(d_ff_1_q[6]), .preset(_6), .reset(clear));  // open: Qn, en
  xor xor_10 (xor_10_out, and_6_out, d_ff_1_q[7]);
  and and_7 (clear, comparator_1_lt, set);
  D_Flip_Flop d_ff_8 (.clk(CLK), .D(xor_10_out), .Q(d_ff_1_q[7]), .preset(_7), .reset(clear));  // open: Qn, en
  xor xor_11 (xor_11_out, or_1_out, PM);
  and _11 (_11_out, ~d_ff_1_q[7], ~d_ff_1_q[6], ~d_ff_1_q[5], ~d_ff_1_q[4], d_ff_1_q[3], ~d_ff_1_q[2], d_ff_1_q[1], d_ff_1_q[0]);  // AND_Gate
  and _23 (_23_out, ~d_ff_1_q[7], ~d_ff_1_q[6], ~d_ff_1_q[5], d_ff_1_q[4], ~d_ff_1_q[3], d_ff_1_q[2], d_ff_1_q[1], d_ff_1_q[0]);  // AND_Gate
  Multiplexer #(.width(8)) multiplexer_1 (
    .in0({8{1'b0}}), .in1(value), .out({_7, _6, _5, _4, _3, _2, _1, _0}), .sel(clear));  // open: en
  D_Flip_Flop d_ff_9 (.clk(CLK), .D(xor_11_out), .Q(PM), .preset(_8), .reset(clear));  // open: Qn, en
  or or_1 (or_1_out, _11_out, _23_out);
  and u__0 (_0_out[2], ~d_ff_1_q[0], ~d_ff_1_q[1], ~d_ff_1_q[2], ~d_ff_1_q[3], ~d_ff_1_q[4], ~d_ff_1_q[5], ~d_ff_1_q[6], ~d_ff_1_q[7]);  // AND_Gate
  // Probe on d_ff_1_q
  xor xor_12 (xor_12_out, CLK, d_ff_10_q);
  D_Flip_Flop d_ff_10 (.clk(xor_12_out), .D(_23_out), .Q(d_ff_10_q));  // open: Qn, preset, en, reset
  Comparator #(.mode("unsigned")) comparator_3 (.a(d_ff_1_q), .b(8'hc), .gt(_0_out[3]));  // open: eq, lt
  and and_8 (Carry, CLK, d_ff_10_q);
  Adder adder_1 (.a(8'hc), .b(d_ff_1_q), .out(adder_1_out));  // open: cin, cout
  Subtractor subtractor_1 (.a(d_ff_1_q), .b(8'hc), .out(subtractor_1_out));  // open: bin, bout
  // Probe on {_0_out, PM, _12_hr}
  // Probe on OUTBITS
  Multiplexer #(.select(4), .width(8)) multiplexer_2 (
    .in0(d_ff_1_q), .in1(d_ff_1_q), .in2(d_ff_1_q), .in3(d_ff_1_q), .in4(d_ff_1_q), .in5(adder_1_out),
    .in8(undriven), .in10(d_ff_1_q), .in11(subtractor_1_out), .out(OUTBITS), .sel({_0_out, PM, _12_hr}));  // open: in6, in7, in9, in12, in13, in14, in15, en

  // Other names for the same wires on the sheet: PM_tunnel = PM
endmodule

module days (
  input  CLK,
  input  PWR,
  input  Leap,
  input  [3:0] Month,
  output Carry,
  output [7:0] OUTBITS
);

  wire _28_out, _29_out, _30_out, _31_out, and_1_out, and_2_out, and_3_out, and_4_out, and_5_out, and_6_out,
       and_7_out, and_8_out, and_9_out, and_11_out, and_12_out, and_13_out, d_ff_9_q, or_1_out, or_2_out,
       or_3_out, or_4_out, or_5_out, start_at_1, xor_1_out, xor_2_out, xor_3_out, xor_4_out, xor_5_out,
       xor_6_out, xor_7_out, xor_8_out, xor_9_out, xor_10_out, xor_11_out, xor_12_out, xor_13_out, xor_14_out;

  xor xor_1 (xor_1_out, PWR, OUTBITS[0]);
  and and_1 (and_1_out, ~Month[0], Month[1], ~Month[2], ~Month[3]);  // AND_Gate
  D_Flip_Flop d_ff_1 (.clk(CLK), .D(xor_1_out), .Q(OUTBITS[0]), .preset(start_at_1));  // open: Qn, en, reset
  D_Flip_Flop d_ff_2 (.clk(CLK), .D(xor_2_out), .Q(OUTBITS[1]));  // open: Qn, preset, en, reset
  xor xor_2 (xor_2_out, xor_3_out, or_3_out);
  xor xor_3 (xor_3_out, OUTBITS[0], OUTBITS[1]);
  and and_2 (and_2_out, OUTBITS[1], OUTBITS[0]);
  xor xor_4 (xor_4_out, xor_5_out, or_4_out);
  xor xor_5 (xor_5_out, and_2_out, OUTBITS[2]);
  D_Flip_Flop d_ff_3 (.clk(CLK), .D(xor_4_out), .Q(OUTBITS[2]));  // open: Qn, preset, en, reset
  and and_3 (and_3_out, OUTBITS[2], OUTBITS[1], OUTBITS[0]);
  D_Flip_Flop d_ff_4 (.clk(CLK), .D(xor_6_out), .Q(OUTBITS[3]));  // open: Qn, preset, en, reset
  xor xor_6 (xor_6_out, xor_7_out, or_4_out);
  xor xor_7 (xor_7_out, and_3_out, OUTBITS[3]);
  and and_4 (and_4_out, OUTBITS[3], OUTBITS[2], OUTBITS[1], OUTBITS[0]);
  and and_5 (and_5_out, Month[0], ~Month[3]);  // AND_Gate
  and and_6 (and_6_out, ~Month[0], ~Month[1], Month[3]);  // AND_Gate
  and and_7 (and_7_out, ~Month[0], ~Month[2], Month[3]);  // AND_Gate
  and and_8 (and_8_out, ~Month[0], Month[2], ~Month[3]);  // AND_Gate
  and and_9 (and_9_out, Month[0], ~Month[2], Month[3]);  // AND_Gate
  and and_10 (start_at_1, PWR, ~OUTBITS[0], ~OUTBITS[1], ~OUTBITS[2], ~OUTBITS[3], ~OUTBITS[4], ~OUTBITS[5], ~OUTBITS[6], ~OUTBITS[7]);  // AND_Gate
  xor xor_8 (xor_8_out, xor_9_out, or_4_out);
  xor xor_9 (xor_9_out, and_4_out, OUTBITS[4]);
  and and_11 (and_11_out, OUTBITS[4], OUTBITS[3], OUTBITS[2], OUTBITS[1], OUTBITS[0]);
  D_Flip_Flop d_ff_5 (.clk(CLK), .D(xor_8_out), .Q(OUTBITS[4]));  // open: Qn, preset, en, reset
  xor xor_10 (xor_10_out, and_11_out, OUTBITS[5]);
  and and_12 (and_12_out, OUTBITS[5], OUTBITS[4], OUTBITS[3], OUTBITS[2], OUTBITS[1], OUTBITS[0]);
  or or_1 (or_1_out, and_5_out, and_6_out, and_7_out);
  or or_2 (or_2_out, and_8_out, and_9_out);
  D_Flip_Flop d_ff_6 (.clk(CLK), .D(xor_11_out), .Q(OUTBITS[5]));  // open: Qn, preset, en, reset
  xor xor_11 (xor_11_out, xor_10_out, _31_out);
  xor xor_12 (xor_12_out, and_12_out, OUTBITS[6]);
  and and_13 (and_13_out, OUTBITS[6], OUTBITS[5], OUTBITS[4], OUTBITS[3], OUTBITS[2], OUTBITS[1], OUTBITS[0]);
  xor xor_13 (xor_13_out, and_13_out, OUTBITS[7]);
  D_Flip_Flop d_ff_7 (.clk(CLK), .D(xor_12_out), .Q(OUTBITS[6]));  // open: Qn, preset, en, reset
  and _31 (_31_out, ~OUTBITS[7], ~OUTBITS[6], ~OUTBITS[5], OUTBITS[4], or_1_out, OUTBITS[3], OUTBITS[2], OUTBITS[1], OUTBITS[0]);  // AND_Gate
  and _30 (_30_out, ~OUTBITS[7], ~OUTBITS[6], ~OUTBITS[5], OUTBITS[4], or_2_out, OUTBITS[3], OUTBITS[2], OUTBITS[1], ~OUTBITS[0]);  // AND_Gate
  D_Flip_Flop d_ff_8 (.clk(CLK), .D(xor_13_out), .Q(OUTBITS[7]));  // open: Qn, preset, en, reset
  and _29 (_29_out, ~OUTBITS[7], ~OUTBITS[6], ~OUTBITS[5], OUTBITS[4], OUTBITS[3], OUTBITS[2], ~OUTBITS[1], OUTBITS[0], and_1_out, Leap);  // AND_Gate
  and _28 (_28_out, ~OUTBITS[7], ~OUTBITS[6], ~OUTBITS[5], OUTBITS[4], OUTBITS[3], OUTBITS[2], ~OUTBITS[1], ~OUTBITS[0], and_1_out, ~Leap);  // AND_Gate
  or or_3 (or_3_out, _30_out, _29_out);
  or or_4 (or_4_out, _30_out, _29_out, _28_out);
  // Probe on OUTBITS
  xor xor_14 (xor_14_out, CLK, d_ff_9_q);
  or or_5 (or_5_out, _31_out, _30_out, _29_out, _28_out);
  and and_14 (Carry, CLK, d_ff_9_q);
  D_Flip_Flop d_ff_9 (.clk(xor_14_out), .D(or_5_out), .Q(d_ff_9_q));  // open: Qn, preset, en, reset

  // Notes on the sheet:
  //   D
  //   C
  //   B
  //   A
  //   Feb
  //   31 day months
  //   30 day months
endmodule

module temp (
  input  [7:0] in_1,
  input  [2:0] in_2,
  input  [7:0] in_3,
  input  [2:0] in_4,
  input  CLK,
  input  CLK_2,
  input  PWR,
  input  PWR_2,
  input  CLK_3,
  input  PWR_3,
  input  CLK_4,
  input  PWR_4,
  input  _24_hr,
  output [7:0] out_14,
  output [7:0] out_15,
  output [7:0] out_16,
  output Leap,
  output Carry,
  output [7:0] OUTBITS,
  output Carry_2,
  output [7:0] OUTBITS_2,
  output [15:0] OUTBITS_3,
  output PM,
  output Carry_3,
  output [7:0] OUTBITS_4
);

  wire _12_out, _12Hr_24Hr_out, _24_out, _59_2_out, _59_out, and_1_out, and_2_out, and_3_out, and_4_out,
       and_5_out, and_6_out, and_7_out, and_9_out, and_10_out, and_11_out, and_12_out, and_13_out,
       and_14_out, and_15_out, and_16_out, and_17_out, and_18_out, and_20_out, and_21_out, and_22_out,
       and_23_out, and_24_out, and_26_out, and_27_out, and_29_out, and_30_out, and_31_out, and_32_out,
       and_33_out, and_34_out, and_35_out, and_36_out, and_37_out, and_38_out, and_39_out, and_40_out,
       and_41_out, and_42_out, \begin , clock_1_out, d_ff_1_q, days_carry, display_1_a, display_1_b,
       display_1_c, display_1_d_2, display_1_e, display_1_f, display_1_g, display_2_a, display_2_b,
       display_2_c, display_2_d_2, display_2_e, display_2_f, display_2_g, Hours_carry, Hours_pm,
       Increase_Days_out, Increase_Hours_out, Increase_Mintues_out, Increase_Month_out, Increase_Years_out,
       minutes_carry, month_carry, or_1_out, or_2_out, or_3_out, or_4_out, or_5_out, seconds_carry,
       start_at_0, start_at_1, xor_1_out, xor_2_out, xor_3_out, xor_4_out, xor_5_out, xor_6_out, xor_7_out,
       xor_8_out, xor_9_out, xor_10_out, xor_11_out, xor_12_out, xor_13_out, xor_14_out, xor_15_out,
       xor_16_out, xor_17_out, xor_18_out, xor_19_out, xor_20_out, xor_21_out, xor_22_out, xor_23_out,
       xor_24_out, xor_25_out, xor_26_out, xor_27_out, xor_28_out, xor_29_out, xor_30_out, xor_31_out,
       xor_32_out, xor_33_out, xor_34_out, xor_35_out, xor_36_out, xor_37_out, xor_38_out, xor_39_out,
       xor_40_out, xor_41_out, xor_42_out, xor_43_out, xor_44_out, xor_45_out, xor_46_out, xor_47_out,
       xor_48_out, xor_49_out, xor_50_out, xor_51_out, xor_52_out, xor_53_out, xor_54_out, xor_55_out,
       year_leap;
  wire [3:0] convert_to_bcd_1__8b_0, convert_to_bcd_1__8b_1, convert_to_bcd_2__8b_0, convert_to_bcd_2__8b_1,
       month_outbits;
  wire [7:0] adder_1_out, adder_2_out, bit_extender_2_out, d_ff_4_q, days_outbits, Hours_outbits,
       minutes_outbits, seconds_outbits, subtractor_1_out;
  wire [11:0] year_outbits;

  Clock clock_1 (.out(clock_1_out));
  Hex_Digit_Display hex_digit_display_1 (.value(convert_to_bcd_1__8b_1));  // open: dp
  Hex_Digit_Display hex_digit_display_2 (.value(convert_to_bcd_1__8b_0));  // open: dp
  Button Increase_Mintues (.out(Increase_Mintues_out));
  seconds seconds (
    .CLK(clock_1_out), .PWR(1'b1), .Carry(seconds_carry), .OUTBITS(seconds_outbits));  // open: value, set
  Button _12Hr_24Hr (.out(_12Hr_24Hr_out));
  xor xor_1 (xor_1_out, 1'b1, d_ff_1_q);
  or or_1 (or_1_out, Increase_Mintues_out, seconds_carry);
  seconds minutes (.CLK(or_1_out), .PWR(1'b1), .Carry(minutes_carry), .OUTBITS(minutes_outbits));  // open: value, set
  // Probe on seconds_outbits
  convert_to_bcd convert_to_bcd_1 (.d(seconds_outbits), ._8b_0(convert_to_bcd_1__8b_0), ._8b_1(convert_to_bcd_1__8b_1));
  Button Increase_Hours (.out(Increase_Hours_out));
  or or_2 (or_2_out, Increase_Hours_out, minutes_carry);
  // Probe on minutes_outbits
  display display_1 (
    .d(convert_to_bcd_1__8b_1), .a(display_1_a), .b(display_1_b), .c(display_1_c), .d_2(display_1_d_2),
    .e(display_1_e), .f(display_1_f), .g(display_1_g));
  display display_2 (
    .d(convert_to_bcd_1__8b_0), .a(display_2_a), .b(display_2_b), .c(display_2_c), .d_2(display_2_d_2),
    .e(display_2_e), .f(display_2_f), .g(display_2_g));
  D_Flip_Flop d_ff_1 (.clk(_12Hr_24Hr_out), .D(xor_1_out), .Q(d_ff_1_q));  // open: Qn, preset, en, reset
  hours Hours (
    .CLK(or_2_out), .PWR(1'b1), ._12_hr(d_ff_1_q), .PM(Hours_pm), .Carry(Hours_carry), .OUTBITS(Hours_outbits));  // open: value, set
  _7_Segment_Display u_7_segment_display_1 (
    .g(display_1_g), .f(display_1_f), .a(display_1_a), .b(display_1_b), .e(display_1_e), .d(display_1_d_2),
    .c(display_1_c));  // open: dp
  _7_Segment_Display u_7_segment_display_2 (
    .g(display_2_g), .f(display_2_f), .a(display_2_a), .b(display_2_b), .e(display_2_e), .d(display_2_d_2),
    .c(display_2_c));  // open: dp
  Shifter shifter_1 (.in(in_1), .\dist (in_2), .out(out_15));
  xor xor_2 (xor_2_out, PWR_2, OUTBITS[0]);
  xor xor_3 (xor_3_out, PWR_3, OUTBITS_2[0]);
  xor xor_4 (xor_4_out, PWR_4, d_ff_4_q[0]);
  Button Increase_Days (.out(Increase_Days_out));
  // Probe on Hours_outbits
  D_Flip_Flop d_ff_2 (.clk(CLK_2), .D(xor_2_out), .Q(OUTBITS[0]));  // open: Qn, preset, en, reset
  D_Flip_Flop d_ff_3 (.clk(CLK_3), .D(xor_3_out), .Q(OUTBITS_2[0]));  // open: Qn, preset, en, reset
  xor xor_5 (xor_5_out, OUTBITS_2[0], OUTBITS_2[1]);
  D_Flip_Flop d_ff_4 (.clk(CLK_4), .D(xor_4_out), .Q(d_ff_4_q[0]), .reset(start_at_0));  // open: Qn, preset, en
  or or_3 (or_3_out, Increase_Days_out, Hours_carry);
  and and_1 (and_1_out, d_ff_1_q, Hours_pm);
  LED u_PM (.in(and_1_out));
  and and_2 (and_2_out, d_ff_1_q, ~Hours_pm);  // AND_Gate
  LED AM (.in(and_2_out));
  xor xor_6 (xor_6_out, OUTBITS[0], OUTBITS[1]);
  D_Flip_Flop d_ff_5 (.clk(CLK_3), .D(xor_5_out), .Q(OUTBITS_2[1]));  // open: Qn, preset, en, reset
  and and_3 (and_3_out, OUTBITS_2[1], OUTBITS_2[0]);
  xor xor_7 (xor_7_out, d_ff_4_q[0], d_ff_4_q[1]);
  Button Increase_Month (.out(Increase_Month_out));
  days days (
    .CLK(or_3_out), .PWR(1'b1), .Leap(year_leap), .Month(month_outbits), .Carry(days_carry),
    .OUTBITS(days_outbits));
  // Probe on days_outbits
  assign out_14 = {{4{1'b0}}, out_15[7:4]};  // Bit_Extender bit_extender_1
  D_Flip_Flop d_ff_6 (.clk(CLK_2), .D(xor_6_out), .Q(OUTBITS[1]));  // open: Qn, preset, en, reset
  xor xor_8 (xor_8_out, xor_9_out, _59_2_out);
  and and_4 (and_4_out, OUTBITS[1], OUTBITS[0]);
  xor xor_9 (xor_9_out, and_4_out, OUTBITS[2]);
  D_Flip_Flop d_ff_7 (.clk(CLK_3), .D(xor_10_out), .Q(OUTBITS_2[2]));  // open: Qn, preset, en, reset
  xor xor_10 (xor_10_out, xor_11_out, _59_out);
  xor xor_11 (xor_11_out, and_3_out, OUTBITS_2[2]);
  D_Flip_Flop d_ff_8 (.clk(CLK_4), .D(xor_7_out), .Q(d_ff_4_q[1]));  // open: Qn, preset, en, reset
  and and_5 (and_5_out, d_ff_4_q[1], d_ff_4_q[0]);
  xor xor_12 (xor_12_out, and_5_out, d_ff_4_q[2]);
  or or_4 (or_4_out, Increase_Month_out, days_carry);
  // Probe on month_outbits
  assign bit_extender_2_out = {{4{1'b0}}, month_outbits};  // Bit_Extender bit_extender_2
  D_Flip_Flop d_ff_9 (.clk(CLK_2), .D(xor_8_out), .Q(OUTBITS[2]));  // open: Qn, preset, en, reset
  and and_6 (and_6_out, OUTBITS[2], OUTBITS[1], OUTBITS[0]);
  xor xor_13 (xor_13_out, xor_14_out, _59_out);
  and and_7 (and_7_out, OUTBITS_2[2], OUTBITS_2[1], OUTBITS_2[0]);
  xor xor_14 (xor_14_out, and_7_out, OUTBITS_2[3]);
  and and_8 (start_at_1, ~_24_hr, ~d_ff_4_q[1], ~d_ff_4_q[2], ~d_ff_4_q[3]);  // AND_Gate
  D_Flip_Flop d_ff_10 (.clk(CLK_4), .D(xor_15_out), .Q(d_ff_4_q[2]));  // open: Qn, preset, en, reset
  xor xor_15 (xor_15_out, xor_12_out, _12_out);
  and and_9 (and_9_out, d_ff_4_q[2], d_ff_4_q[1], d_ff_4_q[0]);
  Button Increase_Years (.out(Increase_Years_out));
  or or_5 (or_5_out, Increase_Years_out, month_carry);
  month month (.Carry(month_carry), .CLK(or_4_out), .PWR(1'b1), .OUTBITS(month_outbits));  // open: value, set
  convert_to_bcd convert_to_bcd_2 (
    .d(bit_extender_2_out), ._8b_0(convert_to_bcd_2__8b_0), ._8b_1(convert_to_bcd_2__8b_1));
  Hex_Digit_Display hex_digit_display_3 (.value(convert_to_bcd_2__8b_0));  // open: dp
  Hex_Digit_Display hex_digit_display_4 (.value(convert_to_bcd_2__8b_1));  // open: dp
  xor xor_16 (xor_16_out, xor_17_out, _59_2_out);
  xor xor_17 (xor_17_out, and_6_out, OUTBITS[3]);
  and and_10 (and_10_out, OUTBITS[3], OUTBITS[2], OUTBITS[1], OUTBITS[0]);
  D_Flip_Flop d_ff_11 (.clk(CLK_3), .D(xor_13_out), .Q(OUTBITS_2[3]));  // open: Qn, preset, en, reset
  and and_11 (and_11_out, OUTBITS_2[3], OUTBITS_2[2], OUTBITS_2[1], OUTBITS_2[0]);
  xor xor_18 (xor_18_out, and_11_out, OUTBITS_2[4]);
  and and_12 (and_12_out, xor_19_out, xor_25_out);
  xor xor_19 (xor_19_out, xor_20_out, _12_out);
  xor xor_20 (xor_20_out, and_9_out, d_ff_4_q[3]);
  and and_13 (and_13_out, d_ff_4_q[3], d_ff_4_q[2], d_ff_4_q[1], d_ff_4_q[0]);
  year year (.CLK(or_5_out), .PWR(1'b1), .OUTBITS(year_outbits), .Leap(year_leap));  // open: value, set
  // Probe on year_outbits
  Adder adder_1 (.a(out_14), .b(in_3), .out(adder_1_out));  // open: cin, cout
  D_Flip_Flop d_ff_12 (.clk(CLK_2), .D(xor_16_out), .Q(OUTBITS[3]));  // open: Qn, preset, en, reset
  xor xor_21 (xor_21_out, xor_22_out, _59_2_out);
  xor xor_22 (xor_22_out, and_10_out, OUTBITS[4]);
  and and_14 (and_14_out, OUTBITS[4], OUTBITS[3], OUTBITS[2], OUTBITS[1], OUTBITS[0]);
  xor xor_23 (xor_23_out, xor_18_out, _59_out);
  and and_15 (and_15_out, OUTBITS_2[4], OUTBITS_2[3], OUTBITS_2[2], OUTBITS_2[1], OUTBITS_2[0]);
  xor xor_24 (xor_24_out, and_15_out, OUTBITS_2[5]);
  D_Flip_Flop d_ff_13 (.clk(CLK_4), .D(and_12_out), .Q(d_ff_4_q[3]));  // open: Qn, preset, en, reset
  xor xor_25 (xor_25_out, xor_20_out, _24_out);
  xor xor_26 (xor_26_out, xor_27_out, _24_out);
  xor xor_27 (xor_27_out, and_13_out, d_ff_4_q[4]);
  and and_16 (and_16_out, d_ff_4_q[4], d_ff_4_q[3], d_ff_4_q[2], d_ff_4_q[1], d_ff_4_q[0]);
  Shifter shifter_2 (.in(adder_1_out), .\dist (in_4), .out(out_16));
  D_Flip_Flop d_ff_14 (.clk(CLK_2), .D(xor_21_out), .Q(OUTBITS[4]));  // open: Qn, preset, en, reset
  xor xor_28 (xor_28_out, and_14_out, OUTBITS[5]);
  and and_17 (and_17_out, OUTBITS[5], OUTBITS[4], OUTBITS[3], OUTBITS[2], OUTBITS[1], OUTBITS[0]);
  D_Flip_Flop d_ff_15 (.clk(CLK_3), .D(xor_23_out), .Q(OUTBITS_2[4]));  // open: Qn, preset, en, reset
  xor xor_29 (xor_29_out, xor_24_out, _59_out);
  and and_18 (and_18_out, OUTBITS_2[5], OUTBITS_2[4], OUTBITS_2[3], OUTBITS_2[2], OUTBITS_2[1], OUTBITS_2[0]);
  and and_19 (start_at_0, ~d_ff_4_q[1], ~d_ff_4_q[1], ~d_ff_4_q[2], d_ff_4_q[3], d_ff_4_q[4]);  // AND_Gate
  D_Flip_Flop d_ff_16 (.clk(CLK_4), .D(xor_26_out), .Q(d_ff_4_q[4]));  // open: Qn, preset, en, reset
  xor xor_30 (xor_30_out, and_16_out, d_ff_4_q[5]);
  D_Flip_Flop d_ff_17 (.clk(CLK_2), .D(xor_31_out), .Q(OUTBITS[5]));  // open: Qn, preset, en, reset
  xor xor_31 (xor_31_out, xor_28_out, _59_2_out);
  xor xor_32 (xor_32_out, and_17_out, OUTBITS[6]);
  D_Flip_Flop d_ff_18 (.clk(CLK_3), .D(xor_29_out), .Q(OUTBITS_2[5]));  // open: Qn, preset, en, reset
  xor xor_33 (xor_33_out, and_18_out, OUTBITS_2[6]);
  and and_20 (and_20_out, OUTBITS_2[6], OUTBITS_2[5], OUTBITS_2[4], OUTBITS_2[3], OUTBITS_2[2], OUTBITS_2[1], OUTBITS_2[0]);
  and and_21 (and_21_out, d_ff_4_q[5], d_ff_4_q[4], d_ff_4_q[3], d_ff_4_q[2], d_ff_4_q[1], d_ff_4_q[0]);
  xor xor_34 (xor_34_out, and_21_out, d_ff_4_q[6]);
  and and_22 (and_22_out, OUTBITS[6], OUTBITS[5], OUTBITS[4], OUTBITS[3], OUTBITS[2], OUTBITS[1], OUTBITS[0]);
  xor xor_35 (xor_35_out, and_22_out, OUTBITS[7]);
  D_Flip_Flop d_ff_19 (.clk(CLK_3), .D(xor_33_out), .Q(OUTBITS_2[6]));  // open: Qn, preset, en, reset
  xor xor_36 (xor_36_out, and_20_out, OUTBITS_2[7]);
  D_Flip_Flop d_ff_20 (.clk(CLK_4), .D(xor_30_out), .Q(d_ff_4_q[5]));  // open: Qn, preset, en, reset
  and and_23 (and_23_out, d_ff_4_q[6], d_ff_4_q[5], d_ff_4_q[4], d_ff_4_q[3], d_ff_4_q[2], d_ff_4_q[1], d_ff_4_q[0]);
  D_Flip_Flop d_ff_21 (.clk(CLK_2), .D(xor_32_out), .Q(OUTBITS[6]));  // open: Qn, preset, en, reset
  D_Flip_Flop d_ff_22 (.clk(CLK_4), .D(xor_34_out), .Q(d_ff_4_q[6]));  // open: Qn, preset, en, reset
  xor xor_37 (xor_37_out, and_23_out, d_ff_4_q[7]);
  D_Flip_Flop d_ff_23 (.clk(CLK_2), .D(xor_35_out), .Q(OUTBITS[7]));  // open: Qn, preset, en, reset
  D_Flip_Flop d_ff_24 (.clk(CLK_3), .D(xor_36_out), .Q(OUTBITS_2[7]));  // open: Qn, preset, en, reset
  and _59 (_59_out, ~OUTBITS_2[7], ~OUTBITS_2[6], OUTBITS_2[5], OUTBITS_2[4], OUTBITS_2[3], ~OUTBITS_2[2], OUTBITS_2[1], OUTBITS_2[0]);  // AND_Gate
  // Probe on OUTBITS_2
  D_Flip_Flop d_ff_25 (.clk(CLK_4), .D(xor_37_out), .Q(d_ff_4_q[7]));  // open: Qn, preset, en, reset
  and _59_2 (_59_2_out, ~OUTBITS[7], ~OUTBITS[6], OUTBITS[5], OUTBITS[4], OUTBITS[3], ~OUTBITS[2], OUTBITS[1], OUTBITS[0]);  // AND_Gate
  and and_24 (and_24_out, CLK_3, _59_out);
  D_Flip_Flop d_ff_26 (.clk(CLK_4), .D(xor_38_out), .Q(PM));  // open: Qn, preset, en, reset
  xor xor_38 (xor_38_out, _12_out, PM);
  and _12 (_12_out, ~d_ff_4_q[7], ~d_ff_4_q[6], ~d_ff_4_q[5], ~d_ff_4_q[4], ~_24_hr, d_ff_4_q[3], d_ff_4_q[2], ~d_ff_4_q[1], ~d_ff_4_q[0]);  // AND_Gate
  and _24 (_24_out, ~d_ff_4_q[7], ~d_ff_4_q[6], ~d_ff_4_q[5], d_ff_4_q[4], _24_hr, d_ff_4_q[3], ~d_ff_4_q[2], ~d_ff_4_q[1], ~d_ff_4_q[0]);  // AND_Gate
  // Probe on d_ff_4_q
  and and_25 (Carry, CLK_2, _59_2_out);
  xor xor_39 (xor_39_out, PWR_3, Carry_2);
  // NOT_Gate not_1 is placed but not wired
  and and_26 (and_26_out, CLK_4, PM, _12_out);
  Adder adder_2 (.a(8'hc), .b(d_ff_4_q), .out(adder_2_out));  // open: cin, cout
  D_Flip_Flop d_ff_27 (.clk(and_24_out), .D(xor_39_out), .Q(Carry_2));  // open: Qn, preset, en, reset
  and and_27 (and_27_out, CLK_4, _24_out);
  Subtractor subtractor_1 (.a(d_ff_4_q), .b(8'h1), .out(subtractor_1_out));  // open: bin, bout
  // AND_Gate and_28 is placed but not wired
  or or_6 (Carry_3, and_26_out, and_27_out);
  // Probe on OUTBITS_4
  Multiplexer #(.select(2), .width(8)) multiplexer_1 ();  // open: in0, in1, in2, in3, out, sel, en
  xor xor_40 (xor_40_out, PWR, OUTBITS_3[0]);
  D_Flip_Flop d_ff_28 (.clk(CLK), .D(xor_40_out), .Q(OUTBITS_3[0]));  // open: Qn, preset, en, reset
  D_Flip_Flop d_ff_29 (.clk(CLK), .D(xor_41_out), .Q(OUTBITS_3[1]));  // open: Qn, preset, en, reset
  xor xor_41 (xor_41_out, OUTBITS_3[0], OUTBITS_3[1]);
  and and_29 (and_29_out, OUTBITS_3[1], OUTBITS_3[0]);
  xor xor_42 (xor_42_out, and_29_out, OUTBITS_3[2]);
  D_Flip_Flop d_ff_30 (.clk(CLK), .D(xor_42_out), .Q(OUTBITS_3[2]), .preset(\begin ));  // open: Qn, en, reset
  and and_30 (and_30_out, OUTBITS_3[2], OUTBITS_3[1], OUTBITS_3[0]);
  xor xor_43 (xor_43_out, and_30_out, OUTBITS_3[3]);
  D_Flip_Flop d_ff_31 (.clk(CLK), .D(xor_43_out), .Q(OUTBITS_3[3]));  // open: Qn, preset, en, reset
  and and_31 (and_31_out, OUTBITS_3[3], OUTBITS_3[2], OUTBITS_3[1], OUTBITS_3[0]);
  xor xor_44 (xor_44_out, and_31_out, OUTBITS_3[4]);
  and and_32 (and_32_out, OUTBITS_3[4], OUTBITS_3[3], OUTBITS_3[2], OUTBITS_3[1], OUTBITS_3[0]);
  D_Flip_Flop d_ff_32 (.clk(CLK), .D(xor_44_out), .Q(OUTBITS_3[4]));  // open: Qn, preset, en, reset
  xor xor_45 (xor_45_out, and_32_out, OUTBITS_3[5]);
  and and_33 (and_33_out, OUTBITS_3[5], OUTBITS_3[4], OUTBITS_3[3], OUTBITS_3[2], OUTBITS_3[1], OUTBITS_3[0]);
  D_Flip_Flop d_ff_33 (.clk(CLK), .D(xor_45_out), .Q(OUTBITS_3[5]), .preset(\begin ));  // open: Qn, en, reset
  xor xor_46 (xor_46_out, and_33_out, OUTBITS_3[6]);
  and and_34 (and_34_out, OUTBITS_3[6], OUTBITS_3[5], OUTBITS_3[4], OUTBITS_3[3], OUTBITS_3[2], OUTBITS_3[1], OUTBITS_3[0]);
  xor xor_47 (xor_47_out, and_34_out, OUTBITS_3[7]);
  and and_35 (and_35_out, OUTBITS_3[7], OUTBITS_3[6], OUTBITS_3[5], OUTBITS_3[4], OUTBITS_3[3], OUTBITS_3[2], OUTBITS_3[1], OUTBITS_3[0]);
  D_Flip_Flop d_ff_34 (.clk(CLK), .D(xor_46_out), .Q(OUTBITS_3[6]), .preset(\begin ));  // open: Qn, en, reset
  xor xor_48 (xor_48_out, and_35_out, OUTBITS_3[8]);
  D_Flip_Flop d_ff_35 (.clk(CLK), .D(xor_47_out), .Q(OUTBITS_3[7]), .preset(\begin ));  // open: Qn, en, reset
  and and_36 (and_36_out, OUTBITS_3[8], OUTBITS_3[7], OUTBITS_3[6], OUTBITS_3[5], OUTBITS_3[4], OUTBITS_3[3], OUTBITS_3[2], OUTBITS_3[1], OUTBITS_3[0]);
  D_Flip_Flop d_ff_36 (.clk(CLK), .D(xor_48_out), .Q(OUTBITS_3[8]), .preset(\begin ));  // open: Qn, en, reset
  xor xor_49 (xor_49_out, and_36_out, OUTBITS_3[9]);
  and and_37 (and_37_out, OUTBITS_3[9], OUTBITS_3[8], OUTBITS_3[7], OUTBITS_3[6], OUTBITS_3[5], OUTBITS_3[4], OUTBITS_3[3], OUTBITS_3[2], OUTBITS_3[1], OUTBITS_3[0]);
  xor xor_50 (xor_50_out, and_37_out, OUTBITS_3[10]);
  and and_38 (and_38_out, OUTBITS_3[10], OUTBITS_3[9], OUTBITS_3[8], OUTBITS_3[7], OUTBITS_3[6], OUTBITS_3[5], OUTBITS_3[4], OUTBITS_3[3], OUTBITS_3[2], OUTBITS_3[1], OUTBITS_3[0]);
  D_Flip_Flop d_ff_37 (.clk(CLK), .D(xor_49_out), .Q(OUTBITS_3[9]), .preset(\begin ));  // open: Qn, en, reset
  xor xor_51 (xor_51_out, and_38_out, OUTBITS_3[11]);
  D_Flip_Flop d_ff_38 (.clk(CLK), .D(xor_50_out), .Q(OUTBITS_3[10]), .preset(\begin ));  // open: Qn, en, reset
  and and_39 (and_39_out, OUTBITS_3[11], OUTBITS_3[10], OUTBITS_3[9], OUTBITS_3[8], OUTBITS_3[7], OUTBITS_3[6], OUTBITS_3[5], OUTBITS_3[4], OUTBITS_3[3], OUTBITS_3[2], OUTBITS_3[1], OUTBITS_3[0]);
  xor xor_52 (xor_52_out, and_39_out, OUTBITS_3[12]);
  D_Flip_Flop d_ff_39 (.clk(CLK), .D(xor_51_out), .Q(OUTBITS_3[11]), .preset(\begin ));  // open: Qn, en, reset
  and and_40 (and_40_out, OUTBITS_3[12], OUTBITS_3[11], OUTBITS_3[10], OUTBITS_3[9], OUTBITS_3[8], OUTBITS_3[7], OUTBITS_3[6], OUTBITS_3[5], OUTBITS_3[4], OUTBITS_3[3], OUTBITS_3[2], OUTBITS_3[1], OUTBITS_3[0]);
  xor xor_53 (xor_53_out, and_40_out, OUTBITS_3[13]);
  and and_41 (and_41_out, OUTBITS_3[13], OUTBITS_3[12], OUTBITS_3[11], OUTBITS_3[10], OUTBITS_3[9], OUTBITS_3[8], OUTBITS_3[7], OUTBITS_3[6], OUTBITS_3[5], OUTBITS_3[4], OUTBITS_3[3], OUTBITS_3[2], OUTBITS_3[1], OUTBITS_3[0]);
  D_Flip_Flop d_ff_40 (.clk(CLK), .D(xor_52_out), .Q(OUTBITS_3[12]), .preset(\begin ));  // open: Qn, en, reset
  xor xor_54 (xor_54_out, and_41_out, OUTBITS_3[14]);
  D_Flip_Flop d_ff_41 (.clk(CLK), .D(xor_53_out), .Q(OUTBITS_3[13]), .preset(\begin ));  // open: Qn, en, reset
  and and_42 (and_42_out, OUTBITS_3[14], OUTBITS_3[13], OUTBITS_3[12], OUTBITS_3[11], OUTBITS_3[10], OUTBITS_3[9], OUTBITS_3[8], OUTBITS_3[7], OUTBITS_3[6], OUTBITS_3[5], OUTBITS_3[4], OUTBITS_3[3], OUTBITS_3[2], OUTBITS_3[1], OUTBITS_3[0]);
  xor xor_55 (xor_55_out, and_42_out, OUTBITS_3[15]);
  and and_43 (\begin , ~OUTBITS_3[15], ~OUTBITS_3[14], ~OUTBITS_3[13], ~OUTBITS_3[12], ~OUTBITS_3[11], ~OUTBITS_3[10], ~OUTBITS_3[9], ~OUTBITS_3[8], ~OUTBITS_3[7], ~OUTBITS_3[6], ~OUTBITS_3[5], ~OUTBITS_3[4], ~OUTBITS_3[3], ~OUTBITS_3[2], ~OUTBITS_3[1], ~OUTBITS_3[0], PWR);  // AND_Gate
  D_Flip_Flop d_ff_42 (.clk(CLK), .D(xor_54_out), .Q(OUTBITS_3[14]), .preset(\begin ));  // open: Qn, en, reset
  D_Flip_Flop d_ff_43 (.clk(CLK), .D(xor_55_out), .Q(OUTBITS_3[15]));  // open: Qn, preset, en, reset
  buf and_44 (Leap, CLK);  // AND_Gate
  // Probe on OUTBITS_3

  // Other names for the same wires on the sheet: PM_tunnel = PM; power = PWR

  // Notes on the sheet:
  //   00 and 10 is keep same (12 hr)
  //   01 is am time and 24hr clock so substract 1
  //   11 is pm and 24hr clock so add 12
endmodule

module year (
  input  CLK,
  input  PWR,
  input  [11:0] value,
  input  set,
  output [11:0] OUTBITS,
  output Leap
);

  wire _0, _0_out, _1, _2, _3, _4, _5, _6, _7, _8, _9, _10, _11, and_1_out, and_2_out, and_3_out, and_4_out,
       and_5_out, and_6_out, and_7_out, and_8_out, and_9_out, and_10_out, \begin , k, not_1_out, or_2_out,
       or_3_out, or_4_out, or_5_out, or_6_out, or_7_out, xor_1_out, xor_2_out, xor_3_out, xor_4_out,
       xor_5_out, xor_6_out, xor_7_out, xor_8_out, xor_9_out, xor_10_out, xor_11_out, xor_12_out;
  wire [11:0] divider_1_rem;

  xor xor_1 (xor_1_out, PWR, OUTBITS[0]);
  or or_1 (k, _1, \begin );
  D_Flip_Flop d_ff_1 (.clk(CLK), .D(xor_1_out), .Q(OUTBITS[0]), .preset(_0), .reset(set));  // open: Qn, en
  D_Flip_Flop d_ff_2 (.clk(CLK), .D(xor_2_out), .Q(OUTBITS[1]), .preset(k), .reset(set));  // open: Qn, en
  xor xor_2 (xor_2_out, OUTBITS[0], OUTBITS[1]);
  and and_1 (and_1_out, OUTBITS[1], OUTBITS[0]);
  xor xor_3 (xor_3_out, and_1_out, OUTBITS[2]);
  D_Flip_Flop d_ff_3 (.clk(CLK), .D(xor_3_out), .Q(OUTBITS[2]), .preset(_2), .reset(set));  // open: Qn, en
  and and_2 (and_2_out, OUTBITS[2], OUTBITS[1], OUTBITS[0]);
  xor xor_4 (xor_4_out, and_2_out, OUTBITS[3]);
  D_Flip_Flop d_ff_4 (.clk(CLK), .D(xor_4_out), .Q(OUTBITS[3]), .preset(_3), .reset(set));  // open: Qn, en
  and and_3 (and_3_out, OUTBITS[3], OUTBITS[2], OUTBITS[1], OUTBITS[0]);
  xor xor_5 (xor_5_out, and_3_out, OUTBITS[4]);
  // Probe on value
  or or_2 (or_2_out, _4, \begin );
  and and_4 (and_4_out, OUTBITS[4], OUTBITS[3], OUTBITS[2], OUTBITS[1], OUTBITS[0]);
  D_Flip_Flop d_ff_5 (.clk(CLK), .D(xor_5_out), .Q(OUTBITS[4]), .preset(or_2_out), .reset(set));  // open: Qn, en
  xor xor_6 (xor_6_out, and_4_out, OUTBITS[5]);
  and and_5 (and_5_out, OUTBITS[5], OUTBITS[4], OUTBITS[3], OUTBITS[2], OUTBITS[1], OUTBITS[0]);
  D_Flip_Flop d_ff_6 (.clk(CLK), .D(xor_6_out), .Q(OUTBITS[5]), .preset(or_3_out), .reset(set));  // open: Qn, en
  or or_3 (or_3_out, _5, \begin );
  xor xor_7 (xor_7_out, and_5_out, OUTBITS[6]);
  and and_6 (and_6_out, OUTBITS[6], OUTBITS[5], OUTBITS[4], OUTBITS[3], OUTBITS[2], OUTBITS[1], OUTBITS[0]);
  xor xor_8 (xor_8_out, and_6_out, OUTBITS[7]);
  D_Flip_Flop d_ff_7 (.clk(CLK), .D(xor_7_out), .Q(OUTBITS[6]), .preset(_6), .reset(set));  // open: Qn, en
  and and_7 (and_7_out, OUTBITS[7], OUTBITS[6], OUTBITS[5], OUTBITS[4], OUTBITS[3], OUTBITS[2], OUTBITS[1], OUTBITS[0]);
  xor xor_9 (xor_9_out, and_7_out, OUTBITS[8]);
  D_Flip_Flop d_ff_8 (.clk(CLK), .D(xor_8_out), .Q(OUTBITS[7]), .preset(or_4_out), .reset(set));  // open: Qn, en
  or or_4 (or_4_out, _7, \begin );
  and and_8 (and_8_out, OUTBITS[8], OUTBITS[7], OUTBITS[6], OUTBITS[5], OUTBITS[4], OUTBITS[3], OUTBITS[2], OUTBITS[1], OUTBITS[0]);
  D_Flip_Flop d_ff_9 (.clk(CLK), .D(xor_9_out), .Q(OUTBITS[8]), .preset(or_5_out), .reset(set));  // open: Qn, en
  or or_5 (or_5_out, _8, \begin );
  xor xor_10 (xor_10_out, and_8_out, OUTBITS[9]);
  and and_9 (and_9_out, OUTBITS[9], OUTBITS[8], OUTBITS[7], OUTBITS[6], OUTBITS[5], OUTBITS[4], OUTBITS[3], OUTBITS[2], OUTBITS[1], OUTBITS[0]);
  xor xor_11 (xor_11_out, and_9_out, OUTBITS[10]);
  Multiplexer #(.width(12)) multiplexer_1 (
    .in0({12{1'b0}}), .in1(value), .out({_11, _10, _9, _8, _7, _6, _5, _4, _3, _2, _1, _0}), .sel(set));  // open: en
  D_Flip_Flop d_ff_10 (.clk(CLK), .D(xor_10_out), .Q(OUTBITS[9]), .preset(or_6_out), .reset(set));  // open: Qn, en
  or or_6 (or_6_out, _9, \begin );
  and and_10 (and_10_out, OUTBITS[10], OUTBITS[9], OUTBITS[8], OUTBITS[7], OUTBITS[6], OUTBITS[5], OUTBITS[4], OUTBITS[3], OUTBITS[2], OUTBITS[1], OUTBITS[0]);
  xor xor_12 (xor_12_out, and_10_out, OUTBITS[11]);
  D_Flip_Flop d_ff_11 (.clk(CLK), .D(xor_11_out), .Q(OUTBITS[10]), .preset(or_7_out), .reset(set));  // open: Qn, en
  or or_7 (or_7_out, _10, \begin );
  and u__0 (_0_out, ~OUTBITS[11], ~OUTBITS[10], ~OUTBITS[9], ~OUTBITS[8], ~OUTBITS[7], ~OUTBITS[6], ~OUTBITS[5], ~OUTBITS[4], ~OUTBITS[3], ~OUTBITS[2], ~OUTBITS[1], ~OUTBITS[0], PWR);  // AND_Gate
  Register #(.width(1)) register_1 (.D(_0_out), .en(not_1_out), .Q(\begin ), .clk(_0_out), .clr(\begin ));
  not not_1 (not_1_out, set);
  D_Flip_Flop d_ff_12 (.clk(CLK), .D(xor_12_out), .Q(OUTBITS[11]), .preset(_11), .reset(set));  // open: Qn, en
  // Probe on OUTBITS
  Divider #(.width(12)) divider_1 (.a(OUTBITS), .b(12'h4), .rem(divider_1_rem));  // open: out, upper
  Comparator #(.width(12)) comparator_1 (.a(divider_1_rem), .b({12{1'b0}}), .eq(Leap));  // open: gt, lt

  // Other names for the same wires on the sheet: clear = set; power = PWR

  // Notes on the sheet:
  //   Probably should have just made this a separate circuit with the comparison being an input
  //   Max is 4095 then rolls back to 2021
endmodule

module month (
  input  CLK,
  input  PWR,
  input  [3:0] value,
  input  set,
  output Carry,
  output [3:0] OUTBITS
);

  wire _0, _1, _2, _3, _12_out, and_1_out, and_3_out, clear, comparator_1_lt, d_ff_5_q, or_1_out, start_at_1,
       xor_1_out, xor_2_out, xor_3_out, xor_4_out, xor_5_out, xor_6_out, xor_7_out;

  xor xor_1 (xor_1_out, PWR, OUTBITS[0]);
  or or_1 (or_1_out, _0, start_at_1);
  D_Flip_Flop d_ff_1 (.clk(CLK), .D(xor_1_out), .Q(OUTBITS[0]), .preset(or_1_out), .reset(clear));  // open: Qn, en
  D_Flip_Flop d_ff_2 (.clk(CLK), .D(xor_2_out), .Q(OUTBITS[1]), .preset(_1), .reset(clear));  // open: Qn, en
  xor xor_2 (xor_2_out, OUTBITS[0], OUTBITS[1]);
  and and_1 (and_1_out, OUTBITS[1], OUTBITS[0]);
  and and_2 (start_at_1, PWR, ~OUTBITS[0], ~OUTBITS[1], ~OUTBITS[2], ~OUTBITS[3]);  // AND_Gate
  xor xor_3 (xor_3_out, xor_4_out, _12_out);
  xor xor_4 (xor_4_out, and_1_out, OUTBITS[2]);
  Comparator #(.width(4), .mode("unsigned")) comparator_1 (
    .a(value), .b(4'b1101), .lt(comparator_1_lt));  // open: gt, eq
  D_Flip_Flop d_ff_3 (.clk(CLK), .D(xor_3_out), .Q(OUTBITS[2]), .preset(_2), .reset(clear));  // open: Qn, en
  and and_3 (and_3_out, OUTBITS[2], OUTBITS[1], OUTBITS[0]);
  D_Flip_Flop d_ff_4 (.clk(CLK), .D(xor_5_out), .Q(OUTBITS[3]), .preset(_3), .reset(clear));  // open: Qn, en
  xor xor_5 (xor_5_out, xor_6_out, _12_out);
  xor xor_6 (xor_6_out, and_3_out, OUTBITS[3]);
  // Probe on OUTBITS
  and _12 (_12_out, OUTBITS[3], OUTBITS[2], ~OUTBITS[1], ~OUTBITS[0]);  // AND_Gate
  and and_4 (clear, comparator_1_lt, set);
  xor xor_7 (xor_7_out, CLK, d_ff_5_q);
  D_Flip_Flop d_ff_5 (.clk(xor_7_out), .D(_12_out), .Q(d_ff_5_q));  // open: Qn, preset, en, reset
  and and_5 (Carry, CLK, d_ff_5_q);
  Multiplexer #(.width(4)) multiplexer_1 (.in0(4'b0000), .in1(value), .out({_3, _2, _1, _0}), .sel(clear));  // open: en
endmodule

module display (
  input  [3:0] d,
  output a,
  output b,
  output c,
  output d_2,
  output e,
  output f,
  output g
);

  wire and_1_out, and_2_out, and_3_out, and_4_out, and_5_out, and_6_out, and_7_out, and_9_out, and_10_out,
       and_11_out, and_12_out, and_13_out, and_14_out, and_15_out, and_16_out, and_17_out, and_18_out,
       and_19_out, and_20_out, and_21_out, and_22_out, and_23_out, and_24_out, and_25_out, not_1_out,
       not_2_out, not_3_out, not_4_out, not_5_out, not_6_out, or_1_out, or_2_out, or_6_out, or_7_out,
       or_10_out, xnor_1_out, xnor_2_out, xnor_3_out, xor_1_out, xor_2_out, xor_3_out;

  not not_1 (not_1_out, d[2]);
  not not_2 (not_2_out, d[2]);
  not not_3 (not_3_out, d[0]);
  not not_4 (not_4_out, d[3]);
  not not_5 (not_5_out, d[3]);
  and and_1 (and_1_out, d[3], not_1_out);
  not not_6 (not_6_out, d[1]);
  xnor xnor_1 (xnor_1_out, d[3], d[0]);
  xnor xnor_2 (xnor_2_out, d[1], d[0]);
  xor xor_1 (xor_1_out, d[3], d[2]);
  and and_2 (and_2_out, ~d[3], or_1_out);  // AND_Gate
  or or_1 (or_1_out, ~d[1], d[0]);  // OR_Gate
  and and_3 (and_3_out, ~d[1], d[0]);  // AND_Gate
  and and_4 (and_4_out, ~d[2], xnor_3_out);  // AND_Gate
  xnor xnor_3 (xnor_3_out, d[1], d[0]);
  and and_5 (and_5_out, d[2], xor_2_out);
  xor xor_2 (xor_2_out, d[1], d[0]);
  and and_6 (and_6_out, ~d[3], ~d[2], d[1]);  // AND_Gate
  and and_7 (and_7_out, ~d[1], d[3]);  // AND_Gate
  or or_2 (or_2_out, ~d[2], d[1]);  // OR_Gate
  and and_8 (e, or_2_out, ~d[0]);  // AND_Gate
  xor xor_3 (xor_3_out, d[3], d[2]);
  and and_9 (and_9_out, ~d[1], ~d[0]);  // AND_Gate
  and and_10 (and_10_out, d[3], d[1]);
  and and_11 (and_11_out, ~d[2], d[1]);  // AND_Gate
  and and_12 (and_12_out, d[1], ~d[0]);  // AND_Gate
  and and_13 (and_13_out, ~d[3], d[2], ~d[1]);  // AND_Gate
  and and_14 (and_14_out, d[3], d[0]);
  and and_15 (and_15_out, d[3], ~d[2]);  // AND_Gate
  and and_16 (and_16_out, not_2_out, not_3_out);
  and and_17 (and_17_out, not_4_out, d[1]);
  and and_18 (and_18_out, not_5_out, d[2]);
  and and_19 (and_19_out, d[2], d[1]);
  and and_20 (and_20_out, and_1_out, not_6_out);
  and and_21 (and_21_out, ~d[1], xnor_1_out);  // AND_Gate
  and and_22 (and_22_out, ~d[3], xnor_2_out);  // AND_Gate
  and and_23 (and_23_out, ~d[3], ~d[2]);  // AND_Gate
  and and_24 (and_24_out, ~d[2], ~d[0]);  // AND_Gate
  or or_3 (c, xor_1_out, and_2_out, and_3_out);
  or or_4 (f, xor_3_out, and_9_out, and_10_out);
  or or_5 (g, and_11_out, and_12_out, and_13_out, and_14_out, and_15_out);
  or or_6 (or_6_out, and_16_out, and_17_out);
  and and_25 (and_25_out, and_18_out, d[0]);
  or or_7 (or_7_out, and_19_out, and_20_out);
  or or_8 (b, and_21_out, and_22_out, and_23_out, and_24_out);
  or or_9 (d_2, and_4_out, and_5_out, and_6_out, and_7_out);
  or or_10 (or_10_out, or_6_out, and_25_out);
  or or_11 (a, or_10_out, or_7_out);
  _7_Segment_Display u_7_segment_display_1 (.g(g), .f(f), .a(a), .b(b), .e(e), .d(d_2), .c(c));  // open: dp

  // Notes on the sheet:
  //   C
  //   A
  //   B
  //   D
  //   C
  //   A
  //   B
  //   A
  //   B
  //   C
  //   A
  //   B
  //   C
  //   D
  //   D
  //   D
endmodule

module convert_to_bcd (
  input  [7:0] d,
  output [3:0] _8b_0,
  output [3:0] _8b_1
);

  ROM rom_1 (.addr(d), .data({_8b_1, _8b_0}));  // open: sel

  // Notes on the sheet:
  //   contents of rom_1 (hex, n*v repeats v):
  //   0 1 2 3 4 5 6 7 8 9 10 11 12 13 14 15 16 17 18 19 20 21 22 23 24 25 26 27 28 29 30 31 32 33 34 35 36
  //   37 38 39 40 41 42 43 44 45 46 47 48 49 50 51 52 53 54 55 56 57 58 59
endmodule

module main (
  input  [11:0] in_1,
  input  [7:0] in_2,
  input  [7:0] in_3,
  input  [7:0] in_4,
  input  [3:0] in_5
);

  wire _12Hr_24Hr_out, and_1_out, and_2_out, clock_1_out, d_ff_1_q, days_carry, hour_out, hours_carry,
       hours_pm, Increase_Day_out, minutes_carry, month_carry, or_1_out, or_2_out, seconds_carry, set_2_out,
       set_3_out, set_4_out, set_5_out, set_out, xor_1_out, year_leap;
  wire [3:0] convert_to_bcd_1__8b_0, convert_to_bcd_1__8b_1, convert_to_bcd_2__8b_0, convert_to_bcd_2__8b_1,
       convert_to_bcd_3__8b_0, convert_to_bcd_3__8b_1, convert_to_bcd_4__8b_0, convert_to_bcd_4__8b_1,
       convert_to_bcd_5__8b_0, convert_to_bcd_5__8b_1, convert_to_bcd_16bit_1__16b_0,
       convert_to_bcd_16bit_1__16b_1, convert_to_bcd_16bit_1__16b_2, convert_to_bcd_16bit_1__16b_3,
       month_outbits;
  wire [7:0] bit_extender_1_out, days_outbits, hours_outbits, minutes_outbits, seconds_outbits;
  wire [11:0] year_outbits;

  Hex_Digit_Display hex_digit_display_1 (.value(convert_to_bcd_16bit_1__16b_3));  // open: dp
  Hex_Digit_Display hex_digit_display_2 (.value(convert_to_bcd_16bit_1__16b_2));  // open: dp
  convert_to_bcd_16bit convert_to_bcd_16bit_1 (
    .e(year_outbits), ._16b_0(convert_to_bcd_16bit_1__16b_0), ._16b_1(convert_to_bcd_16bit_1__16b_1),
    ._16b_2(convert_to_bcd_16bit_1__16b_2), ._16b_3(convert_to_bcd_16bit_1__16b_3));
  Hex_Digit_Display hex_digit_display_3 (.value(convert_to_bcd_16bit_1__16b_0));  // open: dp
  Hex_Digit_Display hex_digit_display_4 (.value(convert_to_bcd_16bit_1__16b_1));  // open: dp
  Button set (.out(set_out));
  year year (.CLK(month_carry), .PWR(1'b1), .OUTBITS(year_outbits), .Leap(year_leap), .value(in_1), .set(set_out));
  Hex_Digit_Display hex_digit_display_5 (.value(convert_to_bcd_1__8b_1));  // open: dp
  Button set_2 (.out(set_2_out));
  month month (
    .Carry(month_carry), .CLK(days_carry), .PWR(1'b1), .OUTBITS(month_outbits), .value(in_5), .set(set_2_out));
  Hex_Digit_Display hex_digit_display_6 (.value(convert_to_bcd_1__8b_0));  // open: dp
  convert_to_bcd convert_to_bcd_1 (
    .d(bit_extender_1_out), ._8b_0(convert_to_bcd_1__8b_0), ._8b_1(convert_to_bcd_1__8b_1));
  assign bit_extender_1_out = {{4{1'b0}}, month_outbits};  // Bit_Extender bit_extender_1
  Hex_Digit_Display hex_digit_display_7 (.value(convert_to_bcd_2__8b_0));  // open: dp
  Hex_Digit_Display hex_digit_display_8 (.value(convert_to_bcd_2__8b_1));  // open: dp
  convert_to_bcd convert_to_bcd_2 (.d(days_outbits), ._8b_0(convert_to_bcd_2__8b_0), ._8b_1(convert_to_bcd_2__8b_1));
  Button Increase_Day (.out(Increase_Day_out));
  days days (
    .CLK(or_1_out), .PWR(1'b1), .Leap(year_leap), .Month(month_outbits), .Carry(days_carry),
    .OUTBITS(days_outbits));
  Hex_Digit_Display hex_digit_display_9 (.value(convert_to_bcd_3__8b_1));  // open: dp
  Hex_Digit_Display hex_digit_display_10 (.value(convert_to_bcd_3__8b_0));  // open: dp
  convert_to_bcd convert_to_bcd_3 (.d(hours_outbits), ._8b_0(convert_to_bcd_3__8b_0), ._8b_1(convert_to_bcd_3__8b_1));
  Button set_3 (.out(set_3_out));
  or or_1 (or_1_out, Increase_Day_out, hours_carry);
  Hex_Digit_Display hex_digit_display_11 (.value(convert_to_bcd_4__8b_1));  // open: dp
  hours hours (
    .CLK(or_2_out), .PWR(1'b1), ._12_hr(d_ff_1_q), .PM(hours_pm), .Carry(hours_carry),
    .OUTBITS(hours_outbits), .value(in_2), .set(set_3_out));
  Hex_Digit_Display hex_digit_display_12 (.value(convert_to_bcd_4__8b_0));  // open: dp
  Hex_Digit_Display hex_digit_display_13 (.value(convert_to_bcd_5__8b_1));  // open: dp
  convert_to_bcd convert_to_bcd_4 (.d(minutes_outbits), ._8b_0(convert_to_bcd_4__8b_0), ._8b_1(convert_to_bcd_4__8b_1));
  Button set_4 (.out(set_4_out));
  seconds minutes (
    .CLK(seconds_carry), .PWR(1'b1), .Carry(minutes_carry), .OUTBITS(minutes_outbits), .value(in_3),
    .set(set_4_out));
  or or_2 (or_2_out, minutes_carry, hour_out);
  Button hour (.out(hour_out));
  blank blank_1 ();
  Hex_Digit_Display hex_digit_display_14 (.value(convert_to_bcd_5__8b_0));  // open: dp
  convert_to_bcd convert_to_bcd_5 (.d(seconds_outbits), ._8b_0(convert_to_bcd_5__8b_0), ._8b_1(convert_to_bcd_5__8b_1));
  seconds seconds (
    .CLK(clock_1_out), .PWR(1'b1), .Carry(seconds_carry), .OUTBITS(seconds_outbits), .value(in_4),
    .set(set_5_out));
  Button _12Hr_24Hr (.out(_12Hr_24Hr_out));
  LED led_1 (.in(and_2_out));
  LED led_2 (.in(and_1_out));
  Button set_5 (.out(set_5_out));
  xor xor_1 (xor_1_out, 1'b1, d_ff_1_q);
  and and_1 (and_1_out, hours_pm, d_ff_1_q);
  and and_2 (and_2_out, d_ff_1_q, ~hours_pm);  // AND_Gate
  Clock clock_1 (.out(clock_1_out));
  D_Flip_Flop d_ff_1 (.clk(_12Hr_24Hr_out), .D(xor_1_out), .Q(d_ff_1_q));  // open: Qn, preset, en, reset
endmodule

module convert_to_bcd_16bit (
  input  [11:0] e,
  output [3:0] _16b_0,
  output [3:0] _16b_1,
  output [3:0] _16b_2,
  output [3:0] _16b_3
);

  ROM #(.addrWidth(12), .dataWidth(16)) rom_1 (.addr(e), .data({_16b_3, _16b_2, _16b_1, _16b_0}));  // open: sel

  // Notes on the sheet:
  //   would crash without this being separate
  //   contents of rom_1 (hex, n*v repeats v):
  //   0 1 2 3 4 5 6 7 8 9 10 11 12 13 14 15 16 17 18 19 20 21 22 23 24 25 26 27 28 29 30 31 32 33 34 35 36
  //   37 38 39 40 41 42 43 44 45 46 47 48 49 50 51 52 53 54 55 56 57 58 59 60 61 62 63 64 65 66 67 68 69
  //   70 71 72 73 74 75 76 77 78 79 80 81 82 83 84 85 86 87 88 89 90 91 92 93 94 95 96 97 98 99 100 101
  //   102 103 104 105 106 107 108 109 110 111 112 113 114 115 116 117 118 119 120 121 122 123 124 125 126
  //   127 128 129 130 131 132 133 134 135 136 137 138 139 140 141 142 143 144 145 146 147 148 149 150 151
  //   152 153 154 155 156 157 158 159 160 161 162 163 164 165 166 167 168 169 170 171 172 173 174 175 176
  //   177 178 179 180 181 182 183 184 185 186 187 188 189 190 191 192 193 194 195 196 197 198 199 200 201
  //   202 203 204 205 206 207 208 209 210 211 212 213 214 215 216 217 218 219 220 221 222 223 224 225 226
  //   227 228 229 230 231 232 233 234 235 236 237 238 239 240 241 242 243 244 245 246 247 248 249 250 251
  //   252 253 254 255 256 257 258 259 260 261 262 263 264 265 266 267 268 269 270 271 272 273 274 275 276
  //   277 278 279 280 281 282 283 284 285 286 287 288 289 290 291 292 293 294 295 296 297 298 299 300 301
  //   302 303 304 305 306 307 308 309 310 311 312 313 314 315 316 317 318 319 320 321 322 323 324 325 326
  //   327 328 329 330 331 332 333 334 335 336 337 338 339 340 341 342 343 344 345 346 347 348 349 350 351
  //   352 353 354 355 356 357 358 359 360 361 362 363 364 365 366 367 368 369 370 371 372 373 374 375 376
  //   377 378 379 380 381 382 383 384 385 386 387 388 389 390 391 392 393 394 395 396 397 398 399 400 401
  //   402 403 404 405 406 407 408 409 410 411 412 413 414 415 416 417 418 419 420 421 422 423 424 425 426
  //   427 428 429 430 431 432 433 434 435 436 437 438 439 440 441 442 443 444 445 446 447 448 449 450 451
  //   452 453 454 455 456 457 458 459 460 461 462 463 464 465 466 467 468 469 470 471 472 473 474 475 476
  //   477 478 479 480 481 482 483 484 485 486 487 488 489 490 491 492 493 494 495 496 497 498 499 500 501
  //   502 503 504 505 506 507 508 509 510 511 512 513 514 515 516 517 518 519 520 521 522 523 524 525 526
  //   527 528 529 530 531 532 533 534 535 536 537 538 539 540 541 542 543 544 545 546 547 548 549 550 551
  //   552 553 554 555 556 557 558 559 560 561 562 563 564 565 566 567 568 569 570 571 572 573 574 575 576
  //   577 578 579 580 581 582 583 584 585 586 587 588 589 590 591 592 593 594 595 596 597 598 599 600 601
  //   602 603 604 605 606 607 608 609 610 611 612 613 614 615 616 617 618 619 620 621 622 623 624 625 626
  //   627 628 629 630 631 632 633 634 635 636 637 638 639 640 641 642 643 644 645 646 647 648 649 650 651
  //   652 653 654 655 656 657 658 659 660 661 662 663 664 665 666 667 668 669 670 671 672 673 674 675 676
  //   677 678 679 680 681 682 683 684 685 686 687 688 689 690 691 692 693 694 695 696 697 698 699 700 701
  //   702 703 704 705 706 707 708 709 710 711 712 713 714 715 716 717 718 719 720 721 722 723 724 725 726
  //   727 728 729 730 731 732 733 734 735 736 737 738 739 740 741 742 743 744 745 746 747 748 749 750 751
  //   752 753 754 755 756 757 758 759 760 761 762 763 764 765 766 767 768 769 770 771 772 773 774 775 776
  //   777 778 779 780 781 782 783 784 785 786 787 788 789 790 791 792 793 794 795 796 797 798 799 800 801
  //   802 803 804 805 806 807 808 809 810 811 812 813 814 815 816 817 818 819 820 821 822 823 824 825 826
  //   827 828 829 830 831 832 833 834 835 836 837 838 839 840 841 842 843 844 845 846 847 848 849 850 851
  //   852 853 854 855 856 857 858 859 860 861 862 863 864 865 866 867 868 869 870 871 872 873 874 875 876
  //   877 878 879 880 881 882 883 884 885 886 887 888 889 890 891 892 893 894 895 896 897 898 899 900 901
  //   902 903 904 905 906 907 908 909 910 911 912 913 914 915 916 917 918 919 920 921 922 923 924 925 926
  //   927 928 929 930 931 932 933 934 935 936 937 938 939 940 941 942 943 944 945 946 947 948 949 950 951
  //   952 953 954 955 956 957 958 959 960 961 962 963 964 965 966 967 968 969 970 971 972 973 974 975 976
  //   977 978 979 980 981 982 983 984 985 986 987 988 989 990 991 992 993 994 995 996 997 998 999 1000
  //   1001 1002 1003 1004 1005 1006 1007 1008 1009 1010 1011 1012 1013 1014 1015 1016 1017 1018 1019 1020
  //   1021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
endmodule
